// Digital circuit somadorLogic.dig as structural Verilog
module somadorLogic (
  input  a,
  input  b
);

  wire u_fullh_carry_out, u_fullh_s_full;

  fullh #(.applicationType("GHDL")) u_fullh (
    .a_full(a), .b_full(b), .s_full(u_fullh_s_full), .carry_out(u_fullh_carry_out));
  LED sum (.in(u_fullh_s_full));
  LED carry (.in(u_fullh_carry_out));
endmodule

/* Test case Teste:
a b sum carry
0 0 0 0
1 0 1 0
0 1 1 0
1 1 0 1
*/

/* Code of fullh:
LIBRARY IEEE;
USE IEEE.std_logic_1164.ALL;

ENTITY fullh IS
    PORT (
        a_full, b_full : IN STD_LOGIC;
        s_full, carry_out : OUT STD_LOGIC
    );
END ENTITY fullh;

ARCHITECTURE comp_full OF fullh IS
    COMPONENT helf2
        PORT (
            a, b : IN STD_LOGIC;
            s, carry : OUT STD_LOGIC
        );
    END COMPONENT;

    SIGNAL s1, c1, c2 : STD_LOGIC;
BEGIN
    ha1 : helf2 PORT MAP(
        a => a_f,
        b => b_f,
        carry => c1,
        s => s1
    );
    ha2 : helf2 PORT MAP(
        a => s1,
        b => carry_in,
        carry => c2,
        s => sum_f
    );
    ----------------------------------------------------------
    ----------------------------------------------------------
    LIBRARY IEEE;
    USE IEEE.std_logic_1164.ALL;

    ENTITY helf2 IS
        PORT (
            a, b : IN STD_LOGIC;
            s, carry : OUT STD_LOGIC
        );
    END ENTITY helf2;

    ARCHITECTURE algoritmo OF somador IS
    BEGIN
        PROCESS (a, b)
        BEGIN
            IF (a = '1' AND b = '0') THEN
                s <= '1';
                carry <= '0';
            ELSIF (a = '0' AND b = '1') THEN
                s <= '1';
                carry <= '0';
            ELSIF (a = '1' AND b = '1') THEN
                s <= '0';
                carry <= '1';
            ELSIF (a = '0' AND b = '0') THEN
                s <= '0';
                carry <= '0';
            END IF;
        END PROCESS;
    END algoritmo;
*/
