// Digital circuit primeiro.dig as structural Verilog
module primeiro (
  input  in_1,
  input  in_2
);

  wire u_primeiro_s;

  primeiro #(.applicationType("GHDL")) u_primeiro (.a(in_1), .b(in_2), .s(u_primeiro_s));
  LED led_1 (.in(u_primeiro_s));
endmodule

/* Code of primeiro:
LIBRARY ieee;
USE IEEE.std_logic_1164.ALL;

ENTITY primeiro IS

    PORT (
        a, b : IN STD_LOGIC;
        s : OUT STD_LOGIC

    );
END ENTITY primeiro;

ARCHITECTURE comp_primeiro OF primeiro IS
BEGIN

    s <= a AND b;

END comp_primeiro;
*/
